# Fritzing sketch BTester (saved by Fritzing 0.9.3b)
breadboards: 2

parts:
  Battery = Screw terminal - 2 pins [package=THT]
  Power_resistor = Screw terminal - 2 pins [package=THT]
  R1 = Resistor [tolerance=±5% resistance=10k package=THT]
  R2 = Resistor [tolerance=±5% resistance=10k package=THT]
  R3 = Resistor [tolerance=±5% resistance=10k package=THT]
  R4 = Resistor [tolerance=±5% resistance=10k package=THT]
  Q1 = Basic FET N-Channel [package="TO220 [THT]"]
  J3 = Piezo Speaker
  U1 = LIPO-1000mAh [package=lipo-1000]
  R5 = Resistor [tolerance=±5% resistance=220 package=THT]
  U2 = PCF8574 [package="DIP16 [THT]"]
  LCD2 = LCD screen
  Q2 = NPN-Transistor [part_number=2N2222 package="TO92 [THT]"]
  Componente3 = Arduino Pro Mini clone (compatible Nano)
  R7 = TRIMPOT [package=trimpot_pth_s3_lock_3386P]
  R8 = Temperature Sensor (Thermistor) [thermistor_type=NTC package=THT]
  R9 = Temperature Sensor (Thermistor) [thermistor_type=NTC package=THT]
  R10 = Resistor [tolerance=±5% resistance=10k package=THT]
  R11 = Resistor [tolerance=±5% resistance=10k package=THT]

nets:
  N1: Battery.pin1, Power_resistor.pin2, R2.Pin_1, U1.+, R5.Pin_0
  GND: Battery.pin2, R1.Pin_0, R4.Pin_0, Q1.source, J3.pin1, U1.-, U2.A0, U2.A1, U2.A3, U2.GND, LCD2.VSS, Q2.C, Componente3.GND, R7.CCW, R10.Pin_0, R11.Pin_1
  N2: Power_resistor.pin1, R3.Pin_1, Q1.drain, R5.Pin_1
  N3: R1.Pin_1, R2.Pin_0, Componente3.A1
  N4: R3.Pin_0, R4.Pin_1, Componente3.A0
  N5: Q1.gate, Componente3.D2
  N6: J3.pin2, Componente3.D9_PWM
  N7: U2.P0, LCD2.DB4
  N8: U2.P1, LCD2.DB5
  N9: U2.P2, LCD2.DB6
  N10: U2.P3, LCD2.DB7
  N11: U2.P4, LCD2.E
  N12: U2.P5, LCD2.R/W
  N13: U2.P6, LCD2.RS
  N14: U2.P7, Q2.B
  N15: U2.SCL, Componente3.A4
  N16: U2.SDA, Componente3.A5
  VCC: U2.VCC, LCD2.VDD, LCD2.LED+, Componente3.VCC, R7.CW, R8.pin_0, R9.pin_1
  N17: LCD2.V0, R7.WIPER
  N18: LCD2.LED-, Q2.E
  N19: Componente3.A3, R9.pin_0, R11.Pin_0
  N20: Componente3.A2, R8.pin_1, R10.Pin_1

notes:
  Indirizzo

custom parts:
  Arduino Pro Mini clone (compatible Nano): It's blue! It's thin! It's the Arduino Pro Mini! SparkFun's minimal design approach to Arduino. New design Pro Mini atmega328 5V 16M Replace ATmega128 Arduino Compatible Nano 1. Arduino-compatible Board. New. 2. ATmega328 running at 16MHz with external resonator (0.5% tolerance) 3. USB connection off board 4. Supports auto-reset 5. Max 150mA output 6. Over current protected 7. Reverse polarity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
  TRIMPOT: Various small potentiometers for set-and-forget applications
