# Fritzing sketch BTesterV02 (saved by Fritzing 0.9.3b)
breadboards: 2

parts:
  For_battery = Screw terminal - 2 pins [package=THT]
  For_power_resistor = Screw terminal - 2 pins [package=THT]
  Resistance_of_power_res_volt_1/2 = Resistor [tolerance=±5% resistance=10k package=THT]
  Resistance_of_power_res_volt_2/2 = Resistor [tolerance=±5% resistance=10k package=THT]
  Resistance_of_battery_volt_2/2 = Resistor [tolerance=±5% resistance=10k package=THT]
  Resistance_of_battery_volt_1/2 = Resistor [tolerance=±5% resistance=10k package=THT]
  IRF744N = Basic FET N-Channel [package="TO220 [THT]"]
  Beeper = Piezo Speaker
  18650_Battery = LIPO-1000mAh [package=lipo-1000]
  Power_resistor = Resistor [tolerance=±5% resistance=10k part_number="Power resistor" package=THT]
  i2c_controller = PCF8574 [package="DIP16 [THT]"]
  Display = LCD screen
  2N2222 = NPN-Transistor [part_number=2N2222 package="TO92 [THT]"]
  Microcontroller = Arduino Pro Mini clone (compatible Nano)
  10K_Trimmer_potentiometer = TRIMPOT [package=trimpot_pth_s3_lock_3386P]
  MF58 = Temperature Sensor (Thermistor) [thermistor_type=NTC package=THT]
  MF58_2 = Temperature Sensor (Thermistor) [thermistor_type=NTC package=THT]
  Thermistor_battery_resistance = Resistor [tolerance=±5% resistance=10k package=THT]
  Thermistor_power_res_resistance = Resistor [tolerance=±5% resistance=10k package=THT]
  Change_button = Pushbutton [package="[THT]"]
  Select_button = Pushbutton [package="[THT]"]
  Reset_button = Pushbutton [package="[THT]"]
  R2 = Resistor [tolerance=±5% resistance=10k package=THT]
  R3 = Resistor [tolerance=±5% resistance=10k package=THT]

nets (from the schematic view):
  N1: For_battery.pin1, For_power_resistor.pin2, Resistance_of_power_res_volt_2/2.Pin_1, 18650_Battery.+, Power_resistor.Pin_0
  GND: For_battery.pin2, Resistance_of_power_res_volt_1/2.Pin_0, Resistance_of_battery_volt_1/2.Pin_0, IRF744N.source, Beeper.pin1, 18650_Battery.-, i2c_controller.A0, i2c_controller.A1, i2c_controller.A3, i2c_controller.GND, 2N2222.C, Thermistor_power_res_resistance.Pin_1, R2.Pin_0, R3.Pin_0
  N2: For_power_resistor.pin1, Resistance_of_battery_volt_2/2.Pin_1, IRF744N.drain, Power_resistor.Pin_1
  N3: Resistance_of_power_res_volt_1/2.Pin_1, Resistance_of_power_res_volt_2/2.Pin_0, Microcontroller.A1
  N4: Resistance_of_battery_volt_2/2.Pin_0, Resistance_of_battery_volt_1/2.Pin_1, Microcontroller.A0
  N5: IRF744N.gate, Microcontroller.D5_PWM
  N6: Beeper.pin2, Microcontroller.D9_PWM
  N7: i2c_controller.P0, Display.DB4
  N8: i2c_controller.P1, Display.DB5
  N9: i2c_controller.P2, Display.DB6
  N10: i2c_controller.P3, Display.DB7
  N11: i2c_controller.P4, Display.E
  N12: i2c_controller.P5, Display.R/W
  N13: i2c_controller.P6, Display.RS
  N14: i2c_controller.P7, 2N2222.B
  N15: i2c_controller.SCL, Microcontroller.A4
  N16: i2c_controller.SDA, Microcontroller.A5
  VCC: i2c_controller.VCC, Display.VDD, Display.LED+, Microcontroller.VCC, 10K_Trimmer_potentiometer.CW, MF58.pin_0, MF58_2.pin_1, Change_button.Pin_3, Change_button.Pin_4, Select_button.Pin_3, Select_button.Pin_4, Reset_button.Pin_3, Reset_button.Pin_4
  VSS: Display.VSS, Microcontroller.GND, 10K_Trimmer_potentiometer.CCW
  N17: Display.V0, 10K_Trimmer_potentiometer.WIPER
  N18: Display.LED-, 2N2222.E
  N19: Microcontroller.A3, MF58_2.pin_0, Thermistor_power_res_resistance.Pin_0
  N20: Microcontroller.A2, MF58.pin_1, Thermistor_battery_resistance.Pin_1
  N21: Change_button.Pin_1, Change_button.Pin_2
  N22: Select_button.Pin_1, Select_button.Pin_2
  N23: Reset_button.Pin_1, Reset_button.Pin_2

notes:
  Indirizzo
  Thermistor on resistance
  Thermistor on battery
  Thermistor circuit
  10k resistor on vcc
  and 10k thermistor.
  Banded pink analog read of battery thermistor, banded orange resistance
  Power resistor analog reading, (10k+10k to support high than 5v)
  Banded bue wire: battery analog reading, (10k+10k to support high than 5v)
  MOSFET to enabled/disable battery drain
  Look at tft project, this part (on this breadboard) can be substituited by a single component

custom parts:
  Arduino Pro Mini clone (compatible Nano): It's blue! It's thin! It's the Arduino Pro Mini! SparkFun's minimal design approach to Arduino. New design Pro Mini atmega328 5V 16M Replace ATmega128 Arduino Compatible Nano 1. Arduino-compatible Board. New. 2. ATmega328 running at 16MHz with external resonator (0.5% tolerance) 3. USB connection off board 4. Supports auto-reset 5. Max 150mA output 6. Over current protected 7. Reverse polarity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
  TRIMPOT: Various small potentiometers for set-and-forget applications
