# Fritzing sketch PTesterV02 (saved by Fritzing 0.9.3b)
perfboards: 1

parts:
  Power_resistor_terminal = Camdenboss CTB0158-2 [part_number="2 Pole 5mm Pitch PCB Mount Screw TermInal Block" package=THT]
  Thermistor_power_resistor = Temperature Sensor (Thermistor) [thermistor_type=NTC part_number=MF58 package=THT]
  Resistor_thermistor = Resistor [tolerance=±5% resistance=10k package=THT]
  Battery_terminal = Camdenboss CTB0158-2 [part_number="2 Pole 5mm Pitch PCB Mount Screw TermInal Block" package=THT]
  MOSFET_to_manage_discharging = Basic FET P-Channel [part_number="IRF744N " package="TO220 [THT]"]
  Resistor_power_voltage_GND_1/2 = Resistor [tolerance=±5% resistance=10k package=THT]
  Resistor_battery_voltage_2/2 = Resistor [tolerance=±5% resistance=10k package=THT]
  Resistor_battery_voltage_GND_1/2 = Resistor [tolerance=±5% resistance=10k package=THT]
  Battery_thermistor_pin = female pin header, 2 pins [form="♀ (female)"]
  Resistor_thermistor_battery = Resistor [tolerance=±5% resistance=10k package=THT]
  PullDown_future_button_1/3 = Resistor [tolerance=±5% resistance=10k package=THT]
  i2c_pin_and_power = female pin header, 4 pins [form="♀ (female)"]
  Right_pin_arduino = female pin header, 11 pins [form="♀ (female)"]
  GND_Reset_VCC_pin = female pin header, 3 pins [form="♀ (female)"]
  Additional_vcc_pin = female pin header, 1 pin [form="♀ (female)"]
  PullDown_change_button = Resistor [tolerance=±5% resistance=10k package=THT]
  ResetGNDbutton = female pin header, 5 pins [form="♀ (female)"]
  Future_pin_10-13 = female pin header, 4 pins [form="♀ (female)"]
  Bottom_pin_arduino = female pin header, 3 pins [form="♀ (female)"]
  Left_pin_arduino = female pin header, 11 pins [form="♀ (female)"]
  Componente1 = Arduino Pro Mini clone (compatible Nano)  # not connected
  PullDown_select_button = Resistor [tolerance=±5% resistance=10k package=THT]
  PullDown_future_button_2/3 = Resistor [tolerance=±5% resistance=10k package=THT]
  PullDown_future_button_3/3 = Resistor [tolerance=±5% resistance=10k package=THT]
  Beeper_male_pin = male pin header, 2 pins [form="♂ (male)"]
  Future_pin_6-8_and_beeper_on_9 = female pin header, 5 pins [form="♀ (female)"]
  Battery_thermistor_male_pin = male pin header, 2 pins [form="♂ (male)"]
  Resistor_power_voltage_2/2 = Resistor [tolerance=±5% resistance=10k package=THT]

nets:
  N1: Power_resistor_terminal.pin1, Battery_terminal.pin1, Resistor_power_voltage_2/2.Pin_1
  N2: Power_resistor_terminal.terminal_2, MOSFET_to_manage_discharging.drain, Resistor_battery_voltage_2/2.Pin_0
  5V: Thermistor_power_resistor.pin_0, Battery_thermistor_pin.pin1, i2c_pin_and_power.pin4, Right_pin_arduino.pin9, GND_Reset_VCC_pin.pin1, Additional_vcc_pin.pin1, Battery_thermistor_male_pin.pin1
  N3: Thermistor_power_resistor.pin_1, Resistor_thermistor.Pin_1, Right_pin_arduino.pin7
  GND: Resistor_thermistor.Pin_0, Battery_terminal.pin2, MOSFET_to_manage_discharging.source, Resistor_power_voltage_GND_1/2.Pin_0, Resistor_battery_voltage_GND_1/2.Pin_0, Resistor_thermistor_battery.Pin_1, PullDown_future_button_1/3.Pin_0, i2c_pin_and_power.pin1, Right_pin_arduino.pin11, GND_Reset_VCC_pin.pin3, PullDown_change_button.Pin_0, Bottom_pin_arduino.pin1, PullDown_select_button.Pin_0, Beeper_male_pin.pin2, Future_pin_6-8_and_beeper_on_9.pin5
  N4: MOSFET_to_manage_discharging.gate, Left_pin_arduino.pin7
  N5: Resistor_power_voltage_GND_1/2.Pin_1, Right_pin_arduino.pin5, Resistor_power_voltage_2/2.Pin_0
  N6: Resistor_battery_voltage_2/2.Pin_1, Resistor_battery_voltage_GND_1/2.Pin_1, Right_pin_arduino.pin6
  N7: Battery_thermistor_pin.pin2, Resistor_thermistor_battery.Pin_0, Right_pin_arduino.pin8, Battery_thermistor_male_pin.pin2
  N8: PullDown_future_button_1/3.Pin_1, ResetGNDbutton.pin5, Left_pin_arduino.pin6
  N9: i2c_pin_and_power.pin2, Bottom_pin_arduino.pin2
  N10: i2c_pin_and_power.pin3, Bottom_pin_arduino.pin3
  N11: Right_pin_arduino.pin1, Future_pin_10-13.pin4
  N12: Right_pin_arduino.pin2, Future_pin_10-13.pin3
  N13: Right_pin_arduino.pin3, Future_pin_10-13.pin2, PullDown_future_button_3/3.Pin_0
  N14: Right_pin_arduino.pin4, Future_pin_10-13.pin1, PullDown_future_button_2/3.Pin_0
  N15: Right_pin_arduino.pin10, GND_Reset_VCC_pin.pin2
  N16: PullDown_change_button.Pin_1, ResetGNDbutton.pin4, Left_pin_arduino.pin5
  N17: ResetGNDbutton.pin1, Left_pin_arduino.pin2
  N18: ResetGNDbutton.pin2, Left_pin_arduino.pin3
  N19: ResetGNDbutton.pin3, Left_pin_arduino.pin4, PullDown_select_button.Pin_1
  N20: Left_pin_arduino.pin8, Future_pin_6-8_and_beeper_on_9.pin1
  N21: Left_pin_arduino.pin9, Future_pin_6-8_and_beeper_on_9.pin2
  N22: Left_pin_arduino.pin10, Future_pin_6-8_and_beeper_on_9.pin3
  N23: Left_pin_arduino.pin11, Beeper_male_pin.pin1, Future_pin_6-8_and_beeper_on_9.pin4
  N24: PullDown_future_button_2/3.Pin_1, PullDown_future_button_3/3.Pin_1

custom parts:
  Arduino Pro Mini clone (compatible Nano): It's blue! It's thin! It's the Arduino Pro Mini! SparkFun's minimal design approach to Arduino. New design Pro Mini atmega328 5V 16M Replace ATmega128 Arduino Compatible Nano 1. Arduino-compatible Board. New. 2. ATmega328 running at 16MHz with external resonator (0.5% tolerance) 3. USB connection off board 4. Supports auto-reset 5. Max 150mA output 6. Over current protected 7. Reverse polarity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
